// Logisim project 7 segment.circ as structural Verilog: 1 circuit, main circuit main
module main (
  input  A,
  input  B,
  input  C,
  input  D,
  output out_5,
  output out_6,
  output out_7,
  output out_8,
  output out_9,
  output out_10,
  output out_11
);

  wire and_1_out, and_2_out, and_3_out, and_4_out, and_5_out, and_6_out, and_7_out, and_8_out, and_9_out,
       not_1_out, not_2_out, not_3_out, not_4_out;

  not not_1 (not_1_out, B);
  not not_2 (not_2_out, A);
  not not_3 (not_3_out, C);
  not not_4 (not_4_out, D);
  and and_1 (and_1_out, B, D);
  and and_2 (and_2_out, not_1_out, not_4_out);
  and and_3 (and_3_out, C, D);
  and and_4 (and_4_out, not_3_out, not_4_out);
  or or_1 (out_7, B, not_3_out, D);
  and and_5 (and_5_out, C, not_4_out);
  and and_6 (and_6_out, not_1_out, C);
  and and_7 (and_7_out, D, and_8_out);
  and and_8 (and_8_out, B, not_3_out);
  and and_9 (and_9_out, B, not_4_out);
  or or_2 (out_5, and_1_out, A, and_2_out, C);
  or or_3 (out_6, and_3_out, not_1_out, and_4_out);
  or or_4 (out_9, and_2_out, and_5_out);
  or or_5 (out_8, and_5_out, and_2_out, and_7_out, A, and_6_out);
  or or_6 (out_10, and_9_out, and_8_out, and_4_out, A);
  or or_7 (out_11, A, and_8_out, and_6_out, and_5_out);
endmodule
